// Logisim project number-guesser-extreme.circ as structural Verilog: 26 circuits, main circuit Cronometro
module Interface (
);

  wire A, A_jogando, A_venceu, \Avançar_A , \Avançar_B , B, B_jogando, B_venceu, C_A, C_B, cfg, empate,
       fim_de_jogo, Iniciar, Jogando_x, Jogando_y, m0a_t, m0b_t, m1a_t, m1b_t, Reset, s0a_t, s0b_t, s1a_t,
       s1b_t, Soma_Certa, tunnel, tunnel_t, X_certo, Y_certo;
  wire [3:0] M0a, M0b, M1a, M1b, PA, PB, S0a, S0b, S1a, S1b, V_A, V_B, X_atual, Y_atual;
  wire [7:0] b_t, r;

  Hex_Digit_Display hex_digit_display_1 (.value(M1a));  // open: dp
  Button button_1 (.out(m1a_t));
  Button button_2 (.out(A));
  Hex_Digit_Display hex_digit_display_2 (.value(PA));  // open: dp
  Hex_Digit_Display hex_digit_display_3 (.value(M0a));  // open: dp
  Button button_3 (.out(m0a_t));
  Hex_Digit_Display hex_digit_display_4 (.value(V_A));  // open: dp
  Button button_4 (.out(C_A));
  LED led_1 (.in(A_jogando));
  LED led_2 (.in(tunnel));
  Hex_Digit_Display hex_digit_display_5 (.value(S0a));  // open: dp
  Hex_Digit_Display hex_digit_display_6 (.value(S1a));  // open: dp
  Button button_5 (.out(s1a_t));
  Button button_6 (.out(s0a_t));
  Button button_7 (.out(\Avançar_A ));
  LED led_3 (.in(X_certo));
  main main_1 (
    .Reset(Reset), .Start(Iniciar), .S0a(s0a_t), .S0b(s0b_t), .S1a(s1a_t), .S1b(s1b_t), .M0a(m0a_t),
    .M0b(m0b_t), .M1a(m1a_t), .M1b(m1b_t), .Advance_A(\Avançar_A ), .Advance_B(\Avançar_B ), .Add_A(A),
    .Add_B(B), .Set_A(C_A), .Set_B(C_B), .Cfg(cfg), .M1a_2(M1a), .M0a_2(M0a), .S1a_2(S1a), .S0a_2(S0a),
    .M1b_2(M1b), .M0b_2(M0b), .S1b_2(S1b), .S0b_2(S0b), .out_26(A_jogando), .out_27(B_jogando), .out_28(V_A),
    .out_29(V_B), .out_30(X_atual), .out_31(Y_atual), .out_32(Jogando_x), .out_33(Jogando_y),
    .out_34(X_certo), .out_35(Y_certo), .out_36(Soma_Certa), .out_37(r), .out_38(b_t), .out_39(PA),
    .out_40(A_venceu), .out_41(PB), .out_42(B_venceu), .out_43(empate), .out_44(fim_de_jogo));
  LED led_4 (.in(A_venceu));
  LED led_5 (.in(Soma_Certa));
  Hex_Digit_Display hex_digit_display_7 (.value(X_atual));  // open: dp
  LED led_6 (.in(Jogando_x));
  Button button_8 (.out(Iniciar));
  LED led_7 (.in(fim_de_jogo));
  LED led_8 (.in(empate));
  // RGBLed #(.multibit("true")) rgbled_1: pin names not known; wires that end beside it: r, b_t
  Hex_Digit_Display hex_digit_display_8 (.value(Y_atual));  // open: dp
  LED led_9 (.in(Jogando_y));
  LED led_10 (.in(cfg));
  Button button_9 (.out(Reset));
  LED led_11 (.in(B_venceu));
  LED led_12 (.in(Y_certo));
  Hex_Digit_Display hex_digit_display_9 (.value(M1b));  // open: dp
  Button button_10 (.out(m1b_t));
  Button button_11 (.out(B));
  Hex_Digit_Display hex_digit_display_10 (.value(PB));  // open: dp
  Hex_Digit_Display hex_digit_display_11 (.value(M0b));  // open: dp
  Button button_12 (.out(m0b_t));
  Hex_Digit_Display hex_digit_display_12 (.value(V_B));  // open: dp
  Button button_13 (.out(C_B));
  LED led_13 (.in(B_jogando));
  LED led_14 (.in(tunnel_t));
  Hex_Digit_Display hex_digit_display_13 (.value(S1b));  // open: dp
  Hex_Digit_Display hex_digit_display_14 (.value(S0b));  // open: dp
  Button button_14 (.out(s0b_t));
  Button button_15 (.out(s1b_t));
  Button button_16 (.out(\Avançar_B ));

  // Notes on the sheet:
  //   Jogador A
  //   PLACAR
  //   CRONÔMETRO
  //   Palpite
  //   Jogador B
  //   PLACAR
  //   CRONÔMETRO
  //   Palpite
endmodule

module main (
  input  Reset,
  input  Start,
  input  S0a,
  input  S0b,
  input  S1a,
  input  S1b,
  input  M0a,
  input  M0b,
  input  M1a,
  input  M1b,
  input  Advance_A,
  input  Advance_B,
  input  Add_A,
  input  Add_B,
  input  Set_A,
  input  Set_B,
  output Cfg,
  output [3:0] M1a_2,
  output [3:0] M0a_2,
  output [3:0] S1a_2,
  output [3:0] S0a_2,
  output [3:0] M1b_2,
  output [3:0] M0b_2,
  output [3:0] S1b_2,
  output [3:0] S0b_2,
  output out_26,
  output out_27,
  output [3:0] out_28,
  output [3:0] out_29,
  output [3:0] out_30,
  output [3:0] out_31,
  output out_32,
  output out_33,
  output out_34,
  output out_35,
  output out_36,
  output [7:0] out_37,
  output [7:0] out_38,
  output [3:0] out_39,
  output out_40,
  output [3:0] out_41,
  output out_42,
  output out_43,
  output out_44
);

  wire a, ada, adb, and_1_out, and_2_out, and_5_out, b, cfgbuttons_1_out_12, cfgbuttons_1_out_13,
       cfgbuttons_1_out_14, cfgbuttons_1_out_15, cfgbuttons_1_out_16, cfgbuttons_1_out_17,
       cfgbuttons_1_out_18, cfgbuttons_1_out_19, cfgbuttons_1_out_20, cfgbuttons_1_out_21, clock_1_out,
       cronometro_1_out_17, cronometro_1_out_18, guesslogic_1_out_7, guesslogic_1_out_8, guesslogic_1_out_9,
       guesslogic_1_out_12, guesslogic_2_out_7, guesslogic_2_out_8, guesslogic_2_out_9, guesslogic_2_out_12,
       hold_3_out_4, hold_4_out_4, hold_5_out_4, hold_6_out_4, hold_7_out_4, multiplexer_3_out,
       multiplexer_4_out, multiplexer_5_out, multiplexer_6_out, multiplexer_7_out, not_1_out, or_1_out,
       playerguess_1_out_12, playerguess_1_out_13, playerguess_1_out_14, playerguess_2_out_12,
       playerguess_2_out_13, playerguess_2_out_14, register_1_q, so;
  wire [3:0] multiplexer_1_out, multiplexer_2_out, playerguess_1_out_10, playerguess_1_out_11,
       playerguess_2_out_10, playerguess_2_out_11;
  wire [7:0] guesslogic_1_out_10, guesslogic_1_out_11, guesslogic_2_out_10, guesslogic_2_out_11,
       multiplexer_8_out, multiplexer_9_out, random_1_out, random_2_out;
  wire [15:0] cfg_1_out_13;

  Hold hold_1 (.in_1(Advance_A), .Clock(clock_1_out), .out_4(ada));  // open: in_3
  Hold hold_2 (.in_1(Advance_B), .Clock(clock_1_out), .out_4(adb));  // open: in_3
  Hold hold_3 (.in_1(Add_A), .Clock(clock_1_out), .out_4(hold_3_out_4));  // open: in_3
  Hold hold_4 (.in_1(Add_B), .Clock(clock_1_out), .out_4(hold_4_out_4));  // open: in_3
  Hold hold_5 (.in_1(Set_A), .in_3(Set_A), .Clock(clock_1_out), .out_4(hold_5_out_4));
  Hold hold_6 (.in_1(Set_B), .Clock(clock_1_out), .out_4(hold_6_out_4));  // open: in_3
  Register #(.width(1), .Select("low")) register_1 (
    .D(1'b1), .en(Start), .Q(register_1_q), .clk(clock_1_out), .clr(or_1_out));
  or or_1 (or_1_out, Reset, out_44);
  Register #(.width(1), .Select("low")) register_2 (.D(1'b1), .en(Start), .Q(so), .clk(clock_1_out), .clr(Reset));
  CfgButtons cfgbuttons_1 (
    .Reset(Reset), .Start(Start), .S0a(S0a), .S0b(S0b), .S1a(S1a), .S1b(S1b), .M0a(M0a), .M0b(M0b),
    .M1a(M1a), .M1b(M1b), .in_11(clock_1_out), .out_12(cfgbuttons_1_out_12), .out_13(cfgbuttons_1_out_13),
    .out_14(cfgbuttons_1_out_14), .out_15(cfgbuttons_1_out_15), .out_16(cfgbuttons_1_out_16),
    .out_17(cfgbuttons_1_out_17), .out_18(cfgbuttons_1_out_18), .out_19(cfgbuttons_1_out_19),
    .out_20(cfgbuttons_1_out_20), .out_21(cfgbuttons_1_out_21));
  Cfg cfg_1 (
    .Reset(cfgbuttons_1_out_12), .Start(cfgbuttons_1_out_13), .S0a(cfgbuttons_1_out_14),
    .S0b(cfgbuttons_1_out_15), .S1a(cfgbuttons_1_out_16), .S1b(cfgbuttons_1_out_17),
    .M0a(cfgbuttons_1_out_18), .M0b(cfgbuttons_1_out_19), .M1a(cfgbuttons_1_out_20),
    .M1b(cfgbuttons_1_out_21), .in_11(clock_1_out), .out_12(Cfg), .out_13(cfg_1_out_13));
  Clock clock_1 (.out(clock_1_out));
  not not_1 (not_1_out, Cfg);
  and and_1 (and_1_out, a, ada);
  and and_2 (and_2_out, b, adb);
  Hold hold_7 (.in_1(register_1_q), .Clock(clock_1_out), .out_4(hold_7_out_4));  // open: in_3
  Cronometro cronometro_1 (
    .Advance_A(and_1_out), .Advance_B(and_2_out), .Enable(not_1_out), .out_9(M1a_2), .out_10(M0a_2),
    .out_11(S1a_2), .out_12(S0a_2), .out_13(M1b_2), .out_14(M0b_2), .out_15(S1b_2), .out_16(S0b_2),
    .Reset(hold_7_out_4), .Clock(clock_1_out), .in_6(cfg_1_out_13), .in_7(cfg_1_out_13), .in_8(out_44),
    .out_18(cronometro_1_out_18), .out_17(cronometro_1_out_17));
  and and_3 (out_26, ~cronometro_1_out_17, register_1_q);  // AND_Gate
  and and_4 (out_27, cronometro_1_out_17, register_1_q);
  PlayerGuess playerguess_1 (
    .Player(cronometro_1_out_17), .in_4(hold_3_out_4), .C(hold_5_out_4), .Adv(ada), .Player_Constant(1'b0),
    .Reset(Reset), .in_7(clock_1_out), .in_8(a), .out_9(out_28), .out_10(playerguess_1_out_10),
    .out_11(playerguess_1_out_11), .out_12(playerguess_1_out_12), .out_13(playerguess_1_out_13),
    .out_14(playerguess_1_out_14));
  PlayerGuess playerguess_2 (
    .Player(cronometro_1_out_17), .in_4(hold_4_out_4), .C(hold_6_out_4), .Adv(adb), .Player_Constant(1'b1),
    .Reset(Reset), .in_7(clock_1_out), .in_8(b), .out_9(out_29), .out_10(playerguess_2_out_10),
    .out_11(playerguess_2_out_11), .out_12(playerguess_2_out_12), .out_13(playerguess_2_out_13),
    .out_14(playerguess_2_out_14));
  and and_5 (and_5_out, cronometro_1_out_18, so);
  Multiplexer #(.width(4), .enable("false")) multiplexer_1 (
    .in0(playerguess_1_out_10), .in1(playerguess_2_out_10), .out(multiplexer_1_out), .sel(cronometro_1_out_17));
  Multiplexer #(.width(4), .enable("false")) multiplexer_2 (
    .in0(playerguess_1_out_11), .in1(playerguess_2_out_11), .out(multiplexer_2_out), .sel(cronometro_1_out_17));
  EndGate_4bits endgate_4bits_1 (.in_1(multiplexer_1_out), .in_2(out_44), .out_3(out_30));
  EndGate_4bits endgate_4bits_2 (.in_1(multiplexer_2_out), .in_2(out_44), .out_3(out_31));
  EndGate endgate_1 (.in_1(multiplexer_3_out), .in_2(out_44), .out_3(out_32));
  Multiplexer #(.enable("false")) multiplexer_3 (
    .in0(playerguess_1_out_12), .in1(playerguess_2_out_12), .out(multiplexer_3_out), .sel(cronometro_1_out_17));
  Multiplexer #(.enable("false")) multiplexer_4 (
    .in0(playerguess_1_out_13), .in1(playerguess_2_out_13), .out(multiplexer_4_out), .sel(cronometro_1_out_17));
  EndGate endgate_2 (.in_1(multiplexer_4_out), .in_2(out_44), .out_3(out_33));
  ScoreTestMode scoretestmode_1 (
    .in_1(playerguess_1_out_14), .in_2(ada), .in_3(clock_1_out), .in_4(Reset), .out_5(a));  // open: out_6
  ScoreTestMode scoretestmode_2 (
    .in_1(playerguess_2_out_14), .in_2(adb), .in_3(clock_1_out), .in_4(Reset), .out_5(b));  // open: out_6
  GuessLogic guesslogic_1 (
    .in_1(a), .in_2(Reset), .X(playerguess_1_out_10), .Y(playerguess_1_out_11), .out_7(guesslogic_1_out_7),
    .out_8(guesslogic_1_out_8), .out_9(guesslogic_1_out_9), .out_10(guesslogic_1_out_10),
    .out_11(guesslogic_1_out_11), .out_12(guesslogic_1_out_12), .in_3(ada), .in_4(random_1_out));
  Random #(.seed(100)) random_1 (.clk(clock_1_out), .next(guesslogic_1_out_12), .out(random_1_out));  // open: clr
  GuessLogic guesslogic_2 (
    .in_1(b), .in_2(Reset), .X(playerguess_2_out_10), .Y(playerguess_2_out_11), .out_7(guesslogic_2_out_7),
    .out_8(guesslogic_2_out_8), .out_9(guesslogic_2_out_9), .out_10(guesslogic_2_out_10),
    .out_11(guesslogic_2_out_11), .out_12(guesslogic_2_out_12), .in_3(adb), .in_4(random_2_out));
  Random random_2 (.clk(clock_1_out), .next(guesslogic_2_out_12), .out(random_2_out));  // open: clr
  Multiplexer #(.enable("false")) multiplexer_5 (
    .in0(guesslogic_1_out_7), .in1(guesslogic_2_out_7), .out(multiplexer_5_out), .sel(cronometro_1_out_17));
  Multiplexer #(.enable("false")) multiplexer_6 (
    .in0(guesslogic_1_out_8), .in1(guesslogic_2_out_8), .out(multiplexer_6_out), .sel(cronometro_1_out_17));
  Multiplexer #(.enable("false")) multiplexer_7 (
    .in0(guesslogic_1_out_9), .in1(guesslogic_2_out_9), .out(multiplexer_7_out), .sel(cronometro_1_out_17));
  Multiplexer #(.width(8), .enable("false")) multiplexer_8 (
    .in0(guesslogic_1_out_10), .in1(guesslogic_2_out_10), .out(multiplexer_8_out), .sel(cronometro_1_out_17));
  Multiplexer #(.width(8), .enable("false")) multiplexer_9 (
    .in0(guesslogic_1_out_11), .in1(guesslogic_2_out_11), .out(multiplexer_9_out), .sel(cronometro_1_out_17));
  EndGate endgate_3 (.in_1(multiplexer_5_out), .in_2(out_44), .out_3(out_34));
  EndGate endgate_4 (.in_1(multiplexer_6_out), .in_2(out_44), .out_3(out_35));
  EndGate endgate_5 (.in_1(multiplexer_7_out), .in_2(out_44), .out_3(out_36));
  EndGate_8bits endgate_8bits_1 (.in_1(multiplexer_8_out), .in_2(out_44), .out_3(out_37));
  EndGate_8bits endgate_8bits_2 (.in_1(multiplexer_9_out), .in_2(out_44), .out_3(out_38));
  Score score_1 (
    .in_2(guesslogic_1_out_7), .in_3(guesslogic_1_out_8), .in_1(ada), .in_4(clock_1_out), .in_5(Reset),
    .out_6(out_39));
  Score score_2 (
    .in_2(guesslogic_2_out_7), .in_3(guesslogic_2_out_8), .in_1(adb), .in_4(clock_1_out), .in_5(Reset),
    .out_6(out_41));
  WinCondition wincondition_1 (.in_1(out_39), .in_2(out_41), .in_3(and_5_out), .out_4(out_40));
  WinCondition wincondition_2 (.in_1(out_41), .in_2(out_39), .in_3(and_5_out), .out_4(out_42));
  and and_6 (out_43, ~out_42, and_5_out, ~out_40);  // AND_Gate
  or or_2 (out_44, and_5_out, out_40, out_42);

  // Other names for the same wires on the sheet: end = out_44; r = Reset
endmodule

module Cfg (
  input  Reset,
  input  Start,
  input  S0a,
  input  S0b,
  input  S1a,
  input  S1b,
  input  M0a,
  input  M0b,
  input  M1a,
  input  M1b,
  input  in_11,
  output out_12,
  output [15:0] out_13
);

  wire or_1_out, or_2_out, or_3_out, or_4_out, or_5_out;
  wire [3:0] cfgvalue_1_out_5, cfgvalue_2_out_5, cfgvalue_3_out_5, cfgvalue_4_out_5;
  wire [15:0] adder_1_out, adder_2_out, bit_extender_1_out, bit_extender_2_out, bit_extender_3_out,
       bit_extender_4_out, multiplier_1_out, multiplier_2_out, multiplier_3_out;

  or or_1 (or_1_out, Reset, Start);
  or or_2 (or_2_out, S0a, S0b);
  or or_3 (or_3_out, S1a, S1b);
  or or_4 (or_4_out, M0a, M0b);
  or or_5 (or_5_out, M1a, M1b);
  Register #(.width(1), .Select("low")) Enabled (.D(Reset), .en(or_1_out), .Q(out_12), .clk(in_11));  // open: clr
  CfgValue cfgvalue_1 (.in_1(out_12), .in_2(or_2_out), .in_3(4'b1001), .in_4(in_11), .out_5(cfgvalue_1_out_5));
  CfgValue cfgvalue_2 (.in_1(out_12), .in_2(or_3_out), .in_3(4'b0101), .in_4(in_11), .out_5(cfgvalue_2_out_5));
  CfgValue cfgvalue_3 (.in_1(out_12), .in_2(or_4_out), .in_3(4'b1001), .in_4(in_11), .out_5(cfgvalue_3_out_5));
  CfgValue cfgvalue_4 (.in_1(out_12), .in_2(or_5_out), .in_3(4'b0101), .in_4(in_11), .out_5(cfgvalue_4_out_5));
  assign bit_extender_1_out = {{12{1'b0}}, cfgvalue_1_out_5};  // Bit_Extender bit_extender_1
  assign bit_extender_2_out = {{12{1'b0}}, cfgvalue_2_out_5};  // Bit_Extender bit_extender_2
  assign bit_extender_3_out = {{12{1'b0}}, cfgvalue_3_out_5};  // Bit_Extender bit_extender_3
  assign bit_extender_4_out = {{12{1'b0}}, cfgvalue_4_out_5};  // Bit_Extender bit_extender_4
  Multiplier #(.width(16)) multiplier_1 (.a(bit_extender_2_out), .b(16'ha), .out(multiplier_1_out));  // open: cin, cout
  Multiplier #(.width(16)) multiplier_2 (
    .a(bit_extender_3_out), .b(16'h3c), .out(multiplier_2_out));  // open: cin, cout
  Multiplier #(.width(16)) multiplier_3 (
    .a(bit_extender_4_out), .b(16'h258), .out(multiplier_3_out));  // open: cin, cout
  Adder #(.width(16)) adder_1 (.a(bit_extender_1_out), .b(multiplier_1_out), .out(adder_1_out));  // open: cin, cout
  Adder #(.width(16)) adder_2 (.a(adder_1_out), .b(multiplier_2_out), .out(adder_2_out));  // open: cin, cout
  Adder #(.width(16)) adder_3 (.a(adder_2_out), .b(multiplier_3_out), .out(out_13));  // open: cin, cout
endmodule

module CfgValue (
  input  in_1,
  input  in_2,
  input  [3:0] in_3,
  input  in_4,
  output [3:0] out_5
);

  wire and_1_out, comparator_1_eq;
  wire [3:0] adder_1_out, multiplexer_1_out;

  and and_1 (and_1_out, in_1, in_2);
  Register #(.width(4), .Select("low")) S0 (.D(multiplexer_1_out), .en(and_1_out), .Q(out_5), .clk(in_4));  // open: clr
  Adder #(.width(4)) adder_1 (.a(4'b0001), .b(out_5), .out(adder_1_out));  // open: cin, cout
  Comparator #(.width(4)) comparator_1 (.a(out_5), .b(in_3), .eq(comparator_1_eq));  // open: gt, lt
  Multiplexer #(.width(4), .enable("false")) multiplexer_1 (
    .in0(adder_1_out), .in1(4'b0000), .out(multiplexer_1_out), .sel(comparator_1_eq));
endmodule

module CfgButtons (
  input  Reset,
  input  Start,
  input  S0a,
  input  S0b,
  input  S1a,
  input  S1b,
  input  M0a,
  input  M0b,
  input  M1a,
  input  M1b,
  input  in_11,
  output out_12,
  output out_13,
  output out_14,
  output out_15,
  output out_16,
  output out_17,
  output out_18,
  output out_19,
  output out_20,
  output out_21
);

  Hold hold_1 (.in_1(Reset), .Clock(in_11), .out_4(out_12));  // open: in_3
  Hold hold_2 (.in_1(Start), .Clock(in_11), .out_4(out_13));  // open: in_3
  Hold hold_3 (.in_1(S0a), .Clock(in_11), .out_4(out_14));  // open: in_3
  Hold hold_4 (.in_1(S0b), .Clock(in_11), .out_4(out_15));  // open: in_3
  Hold hold_5 (.in_1(S1a), .Clock(in_11), .out_4(out_16));  // open: in_3
  Hold hold_6 (.in_1(S1b), .Clock(in_11), .out_4(out_17));  // open: in_3
  Hold hold_7 (.in_1(M0a), .Clock(in_11), .out_4(out_18));  // open: in_3
  Hold hold_8 (.in_1(M0b), .Clock(in_11), .out_4(out_19));  // open: in_3
  Hold hold_9 (.in_1(M1a), .Clock(in_11), .out_4(out_20));  // open: in_3
  Hold hold_10 (.in_1(M1b), .Clock(in_11), .out_4(out_21));  // open: in_3
endmodule

module PlayerGuess (
  input  Player,
  input  Player_Constant,
  input  Reset,
  input  in_4,
  input  C,
  input  Adv,
  input  in_7,
  input  in_8,
  output [3:0] out_9,
  output [3:0] out_10,
  output [3:0] out_11,
  output out_12,
  output out_13,
  output out_14
);

  wire and_1_out, and_2_out, and_3_out, and_6_out, and_7_out, comparator_1_eq, not_1_out, or_1_out, or_2_out,
       register_1_q, register_2_q, register_3_q;
  wire [3:0] adder_1_out;

  Register #(.width(1), .Select("low")) register_1 (.D(or_1_out), .Q(register_1_q), .clk(in_7), .clr(Adv));  // open: en
  Register #(.width(1), .Select("low")) register_2 (.D(or_2_out), .Q(register_2_q), .clk(in_7), .clr(Adv));  // open: en
  Comparator #(.width(1)) comparator_1 (.a(Player_Constant), .b(Player), .eq(comparator_1_eq));  // open: gt, lt
  or or_1 (or_1_out, C, register_1_q);
  or or_2 (or_2_out, C, register_2_q);
  and and_1 (and_1_out, comparator_1_eq, ~in_8, in_4);  // AND_Gate
  and and_2 (and_2_out, comparator_1_eq, ~in_8, C);  // AND_Gate
  not not_1 (not_1_out, register_3_q);
  and and_3 (and_3_out, comparator_1_eq, ~in_8, Adv);  // AND_Gate
  and and_4 (out_12, comparator_1_eq, ~register_3_q, register_1_q);  // AND_Gate
  and and_5 (out_13, comparator_1_eq, register_3_q, register_2_q);
  Register #(.width(1), .Select("low")) register_3 (
    .D(not_1_out), .en(and_3_out), .Q(register_3_q), .clk(in_7), .clr(in_8));
  Register #(.width(4), .Select("low")) register_4 (
    .D(adder_1_out), .en(and_1_out), .Q(out_9), .clk(in_7), .clr(Reset));
  and and_6 (and_6_out, and_2_out, ~register_3_q);  // AND_Gate
  and and_7 (and_7_out, and_2_out, register_3_q);
  Adder #(.width(4)) adder_1 (.a(out_9), .b(4'b0001), .out(adder_1_out));  // open: cin, cout
  Register #(.width(4), .Select("low")) register_5 (.D(out_9), .en(and_6_out), .Q(out_10), .clk(in_7), .clr(Reset));
  Register #(.width(4), .Select("low")) register_6 (.D(out_9), .en(and_7_out), .Q(out_11), .clk(in_7), .clr(Reset));
  Wait wait_1 (.in_1(register_3_q), .in_2(in_7), .out_3(out_14));
endmodule

module ResetCondition (
  input  in_1,
  input  in_2,
  input  in_3,
  input  in_4,
  output out_5
);

  wire and_1_out, and_2_out;

  and and_1 (and_1_out, in_1, in_2);
  and and_2 (and_2_out, and_1_out, in_4);
  or or_1 (out_5, in_3, and_2_out);
endmodule

module GuessLogic (
  input  in_1,
  input  in_2,
  input  in_3,
  input  [7:0] in_4,
  input  [3:0] X,
  input  [3:0] Y,
  output out_7,
  output out_8,
  output out_9,
  output [7:0] out_10,
  output [7:0] out_11,
  output out_12
);

  wire comparator_1_eq, comparator_2_eq, comparator_3_eq;
  wire [4:0] \diferença_1_out_3 , somador_1_out_3, somador_2_out_3;
  wire [7:0] bit_extender_1_out, cores_1_out_2, cores_1_out_3;

  ResetCondition resetcondition_1 (.in_1(out_7), .in_2(out_8), .in_3(in_2), .in_4(in_3), .out_5(out_12));
  assign bit_extender_1_out = {{7{in_1}}, in_1};  // Bit_Extender bit_extender_1
  somador somador_1 (.in_1(X), .in_2(Y), .out_3(somador_1_out_3));
  and and_1 (out_7, in_1, comparator_1_eq);
  Comparator #(.width(4)) comparator_1 (.a(in_4[3:0]), .b(X), .eq(comparator_1_eq));  // open: gt, lt
  somador somador_2 (.in_1(in_4[7:4]), .in_2(in_4[3:0]), .out_3(somador_2_out_3));
  and and_2 (out_8, in_1, comparator_2_eq);
  Comparator #(.width(4)) comparator_2 (.a(in_4[7:4]), .b(Y), .eq(comparator_2_eq));  // open: gt, lt
  and and_3 (out_9, in_1, comparator_3_eq);
  Comparator #(.width(5)) comparator_3 (
    .a(somador_2_out_3), .b(somador_1_out_3), .eq(comparator_3_eq));  // open: gt, lt
  assign out_10 = bit_extender_1_out & cores_1_out_2;  // AND_Gate and_4, 8 bits wide
  \diferença  \diferença_1  (.in_1(somador_2_out_3), .in_2(somador_1_out_3), .out_3(\diferença_1_out_3 ));
  assign out_11 = cores_1_out_3 & bit_extender_1_out;  // AND_Gate and_5, 8 bits wide
  cores cores_1 (.out_2(cores_1_out_2), .out_3(cores_1_out_3), .in_1(\diferença_1_out_3 ));
endmodule

module ScoreTestMode (
  input  in_1,
  input  in_2,
  input  in_3,
  input  in_4,
  output out_5,
  output out_6
);

  wire and_1_out, not_1_out, or_1_out;

  or or_1 (or_1_out, out_5, in_1);
  Register #(.width(1), .Select("low")) register_1 (.D(not_1_out), .en(and_1_out), .Q(out_5), .clk(in_3), .clr(in_4));
  and and_1 (and_1_out, or_1_out, in_2);
  not not_1 (not_1_out, out_5);
  and and_2 (out_6, out_5, in_2);
endmodule

module Cronometro (
  input  Advance_A,
  input  Advance_B,
  input  Enable,
  input  Reset,
  input  Clock,
  input  [15:0] in_6,
  input  [15:0] in_7,
  input  in_8,
  output [3:0] out_9,
  output [3:0] out_10,
  output [3:0] out_11,
  output [3:0] out_12,
  output [3:0] out_13,
  output [3:0] out_14,
  output [3:0] out_15,
  output [3:0] out_16,
  output out_17,
  output out_18
);

  wire changeplayer_1_out_6, not_1_out, not_2_out, playercronometergatea_1_out_5,
       playercronometergateb_1_out_5, playertime_1_out_10, playertime_2_out_10;

  not not_1 (not_1_out, out_17);
  PlayerTime playertime_1 (
    .Cfg(Enable), .IsPlayer(not_1_out), .PChange(changeplayer_1_out_6), .M1(out_9), .M0(out_10), .S1(out_11),
    .S0(out_12), .Clock(playercronometergatea_1_out_5), .t(in_6), .out_10(playertime_1_out_10));
  not not_2 (not_2_out, out_17);
  ChangePlayer changeplayer_1 (
    .Player(out_17), .A_Time_Zero(playertime_1_out_10), .B_Time_Zero(playertime_2_out_10),
    .A_Advance(Advance_A), .B_Advance(Advance_B), .out_6(changeplayer_1_out_6));
  Register #(.width(1), .Select("low")) register_1 (
    .D(not_2_out), .en(changeplayer_1_out_6), .Q(out_17), .clk(Clock), .clr(Reset));
  PlayerCronometerGateA playercronometergatea_1 (
    .out_5(playercronometergatea_1_out_5), .in_2(Clock), .in_3(out_17), .in_4(Enable), .in_1(in_8));
  PlayerTime playertime_2 (
    .Cfg(Enable), .IsPlayer(out_17), .PChange(changeplayer_1_out_6), .M1(out_13), .M0(out_14), .S1(out_15),
    .S0(out_16), .Clock(playercronometergateb_1_out_5), .t(in_7), .out_10(playertime_2_out_10));
  and and_1 (out_18, playertime_2_out_10, playertime_1_out_10);
  PlayerCronometerGateB playercronometergateb_1 (
    .out_5(playercronometergateb_1_out_5), .in_2(Clock), .in_3(out_17), .in_4(Enable), .in_1(in_8));
endmodule

module PlayerTime (
  input  Clock,
  input  [15:0] t,
  input  Cfg,
  input  IsPlayer,
  input  PChange,
  output [3:0] M1,
  output [3:0] M0,
  output [3:0] S1,
  output [3:0] S0,
  output out_10
);

  wire and_1_out, or_1_out, slowclock_1_out_2;
  wire [0:0] not_2_out;
  wire [1:0] subtractor_1_bout;
  wire [15:0] divider_1_rem, divider_2_rem, multiplexer_1_out, multiplexer_2_out, register_1_q,
       subtractor_1_out;
  wire [15:4] divider_1_out, divider_2_out, divider_3_out, divider_3_rem;

  SlowClock slowclock_1 (.out_2(slowclock_1_out_2), .in_1(Clock));
  not not_1 (subtractor_1_bout[1], Cfg);
  not not_2 (not_2_out[0], IsPlayer);
  and and_1 (and_1_out, PChange, Clock);
  Register #(.width(16), .Select("low")) register_1 (
    .D(multiplexer_1_out), .Q(register_1_q), .clk(or_1_out));  // open: en, clr
  or or_1 (or_1_out, slowclock_1_out_2, and_1_out);
  Comparator #(.width(16)) comparator_1 (.a(register_1_q), .b({16{1'b0}}), .eq(out_10));  // open: gt, lt
  Subtractor #(.width(16)) subtractor_1 (
    .a(register_1_q), .b(16'h1), .out(subtractor_1_out), .bout(subtractor_1_bout[0]));  // open: bin
  Multiplexer #(.select(2), .width(16), .enable("false")) multiplexer_1 (
    .in0(subtractor_1_out), .in1({16{1'b0}}), .in2(t), .in3(t), .out(multiplexer_1_out),
    .sel(subtractor_1_bout));
  Multiplexer #(.select(2), .width(16), .enable("false")) multiplexer_2 (
    .in0(register_1_q), .in1(register_1_q), .in2(t), .in3(t), .out(multiplexer_2_out),
    .sel({subtractor_1_bout[1], not_2_out[0]}));
  Divider #(.width(16)) divider_1 (
    .a(multiplexer_2_out), .b(16'h258), .out({divider_1_out, M1}), .rem(divider_1_rem));  // open: upper
  Divider #(.width(16)) divider_2 (
    .a(divider_1_rem), .b(16'h3c), .out({divider_2_out, M0}), .rem(divider_2_rem));  // open: upper
  Divider #(.width(16)) divider_3 (
    .a(divider_2_rem), .b(16'ha), .out({divider_3_out, S1}), .rem({divider_3_rem, S0}));  // open: upper

  // Other names for the same wires on the sheet: a[3:0] = M1; b[3:0] = M0; d[3:0] = S0; c[3:0] = S1
endmodule

module ChangePlayer (
  input  Player,
  input  A_Time_Zero,
  input  B_Time_Zero,
  input  A_Advance,
  input  B_Advance,
  output out_6
);

  wire and_1_out, and_2_out, and_3_out, and_4_out, or_1_out, or_2_out;

  and and_1 (and_1_out, ~Player, A_Time_Zero);  // AND_Gate
  or or_1 (or_1_out, and_1_out, and_2_out);
  and and_2 (and_2_out, ~Player, A_Advance);  // AND_Gate
  and and_3 (and_3_out, Player, B_Time_Zero);
  or or_2 (or_2_out, and_3_out, and_4_out);
  and and_4 (and_4_out, Player, B_Advance);
  or or_3 (out_6, or_1_out, or_2_out);
endmodule

module PlayerCronometerGateA (
  input  in_1,
  input  in_2,
  input  in_3,
  input  in_4,
  output out_5
);

  wire or_1_out;

  and and_1 (out_5, in_2, ~in_1, or_1_out);  // AND_Gate
  or or_1 (or_1_out, ~in_3, ~in_4);  // OR_Gate
endmodule

module PlayerCronometerGateB (
  input  in_1,
  input  in_2,
  input  in_3,
  input  in_4,
  output out_5
);

  wire or_1_out;

  and and_1 (out_5, in_2, ~in_1, or_1_out);  // AND_Gate
  or or_1 (or_1_out, in_3, ~in_4);  // OR_Gate
endmodule

module somador (
  input  [3:0] in_1,
  input  [3:0] in_2,
  output [4:0] out_3
);

  Adder #(.width(4)) adder_1 (.a(in_1), .b(in_2), .out(out_3[3:0]), .cout(out_3[4]));  // open: cin
endmodule

module \diferença  (
  input  [4:0] in_1,
  input  [4:0] in_2,
  output [4:0] out_3
);

  wire subtractor_1_bout;
  wire [4:0] subtractor_1_out, subtractor_2_out;

  Subtractor #(.width(5)) subtractor_1 (
    .a(in_1), .b(in_2), .out(subtractor_1_out), .bout(subtractor_1_bout));  // open: bin
  Subtractor #(.width(5)) subtractor_2 (.a(in_2), .b(in_1), .out(subtractor_2_out));  // open: bin, bout
  Multiplexer #(.width(5), .enable("false")) multiplexer_1 (
    .in0(subtractor_1_out), .in1(subtractor_2_out), .out(out_3), .sel(subtractor_1_bout));
endmodule

module cores (
  input  [4:0] in_1,
  output [7:0] out_2,
  output [7:0] out_3
);

  assign out_2 = ~{in_1, 3'b111};  // NOT_Gate not_1, 8 bits wide

  assign out_3 = {in_1, 3'b111};
endmodule

module Hold (
  input  in_1,
  input  Clock,
  input  in_3,
  output out_4
);

  wire and_1_out, and_2_out, not_1_out, or_1_out, X_q, Y_q;

  not not_1 (not_1_out, in_1);
  Register #(.width(1), .Select("low")) X (.D(not_1_out), .en(Y_q), .Q(X_q), .clk(Clock), .clr(in_3));
  and and_1 (and_1_out, in_1, X_q);
  or or_1 (or_1_out, in_1, Y_q);
  Register #(.width(1), .Select("low")) Y (.D(or_1_out), .Q(Y_q), .clk(Clock), .clr(in_3));  // open: en
  and and_2 (and_2_out, in_1, ~Y_q);  // AND_Gate
  or or_2 (out_4, and_1_out, and_2_out);
endmodule

module SlowClock (
  input  in_1,
  output out_2
);

  wire [7:0] counter_1_q;

  Counter #(.max('h20)) counter_1 (.Q(counter_1_q), .clk(in_1));  // open: load, D, count, carry, clr, preset, down
  and and_1 (out_2, ~counter_1_q[0], ~counter_1_q[1], ~counter_1_q[2], ~counter_1_q[3], ~counter_1_q[4], ~counter_1_q[5], ~counter_1_q[6], ~counter_1_q[7]);  // AND_Gate
endmodule

module Wait_16bits (
  input  [15:0] in_1,
  input  in_2,
  output [15:0] out_3
);

  wire not_1_out, not_2_out, register_3_q;
  wire [15:0] register_1_q, register_2_q;

  Register #(.width(16), .Select("low")) register_1 (
    .D(in_1), .en(register_3_q), .Q(register_1_q), .clk(in_2));  // open: clr
  Register #(.width(16), .Select("low")) register_2 (
    .D(in_1), .en(not_1_out), .Q(register_2_q), .clk(in_2));  // open: clr
  not not_1 (not_1_out, register_3_q);
  Register #(.width(1), .Select("low")) register_3 (.D(not_2_out), .Q(register_3_q), .clk(in_2));  // open: en, clr
  not not_2 (not_2_out, register_3_q);
  Multiplexer #(.width(16), .enable("false")) multiplexer_1 (
    .in0(register_2_q), .in1(register_1_q), .out(out_3), .sel(register_3_q));
endmodule

module Wait (
  input  in_1,
  input  in_2,
  output out_3
);

  wire not_1_out, not_2_out, register_1_q, register_2_q, register_3_q;

  not not_1 (not_1_out, register_3_q);
  Register #(.width(1), .Select("low")) register_1 (
    .D(in_1), .en(register_3_q), .Q(register_1_q), .clk(in_2));  // open: clr
  Register #(.width(1), .Select("low")) register_2 (
    .D(in_1), .en(not_1_out), .Q(register_2_q), .clk(in_2));  // open: clr
  not not_2 (not_2_out, register_3_q);
  Register #(.width(1), .Select("low")) register_3 (.D(not_2_out), .Q(register_3_q), .clk(in_2));  // open: en, clr
  Multiplexer #(.enable("false")) multiplexer_1 (
    .in0(register_2_q), .in1(register_1_q), .out(out_3), .sel(register_3_q));
endmodule

module Score (
  input  in_1,
  input  in_2,
  input  in_3,
  input  in_4,
  input  in_5,
  output [3:0] out_6
);

  wire and_1_out;
  wire [3:0] adder_1_out;

  and and_1 (and_1_out, in_2, in_1, in_3);
  Register #(.width(4), .Select("low")) register_1 (.D(adder_1_out), .en(and_1_out), .Q(out_6), .clk(in_4), .clr(in_5));
  Adder #(.width(4)) adder_1 (.a(out_6), .b(4'b0001), .out(adder_1_out));  // open: cin, cout
endmodule

module WinCondition (
  input  [3:0] in_1,
  input  [3:0] in_2,
  input  in_3,
  output out_4
);

  wire and_1_out, comparator_1_gt, comparator_2_eq;

  Comparator #(.width(4), .mode("unsigned")) comparator_1 (.a(in_1), .b(in_2), .gt(comparator_1_gt));  // open: eq, lt
  Comparator #(.width(4), .mode("unsigned")) comparator_2 (
    .a(in_1), .b(4'b1111), .eq(comparator_2_eq));  // open: gt, lt
  or or_1 (out_4, and_1_out, comparator_2_eq);
  and and_1 (and_1_out, comparator_1_gt, in_3);
endmodule

module EndGate (
  input  in_1,
  input  in_2,
  output out_3
);

  and and_1 (out_3, in_1, ~in_2);  // AND_Gate
endmodule

module EndGate_4bits (
  input  [3:0] in_1,
  input  in_2,
  output [3:0] out_3
);

  wire [3:0] bit_extender_1_out;

  assign bit_extender_1_out = {{3{in_2}}, in_2};  // Bit_Extender bit_extender_1
  assign out_3 = in_1 & ~bit_extender_1_out;  // AND_Gate and_1, 4 bits wide
endmodule

module EndGate_8bits (
  input  [7:0] in_1,
  input  in_2,
  output [7:0] out_3
);

  wire [7:0] bit_extender_1_out;

  assign bit_extender_1_out = {{7{in_2}}, in_2};  // Bit_Extender bit_extender_1
  assign out_3 = in_1 & ~bit_extender_1_out;  // AND_Gate and_1, 8 bits wide
endmodule
